# Fritzing sketch Plan (saved by Fritzing 0.9.3b)
breadboards: 1

parts:
  Bauteil1 = Arduino Nano (Rev3.0)
  U1 = RF-LINK_TX [package=rf-link_tx]

nets:
  N1: Bauteil1.D10, U1.DATA
  5V: Bauteil1.5V, U1.+5V
